# Fritzing sketch Fritzing Pinout (saved by Fritzing 0.9.10b)

parts:
  Part1 = BH1750
  Part2 = Arduino Uno (Rev3) - ICSP
  LCD2004-I2C1 = LCD2004-I2C
  HC-SR04_Sensor_1 = HC-SR04 Ultrasonic Distance Sensor

nets:
  VCC: Part1.VCC, Part2.5V, LCD2004-I2C1.VCC, HC-SR04_Sensor_1.VCC
  GND: Part1.GND, Part2.GND, HC-SR04_Sensor_1.GND
  N1: Part1.SCL, Part2.A5/SCL, LCD2004-I2C1.SCL
  N2: Part1.SDA, Part2.A4/SDA, LCD2004-I2C1.SDA
  N3: Part2.D11_PWM/MOSI, HC-SR04_Sensor_1.TRIG
  N4: Part2.D12/MISO, HC-SR04_Sensor_1.ECHO

custom parts:
  BH1750: Light Sensor
  LCD2004-I2C: A standard character display with 4x20 characters. Comes in many colors with LCM2004 IIC attached.
